// Logisim project 2° PFO Sebastian Puche Circuito.circ as structural Verilog
module Sumador (
  input  in_1,
  input  in_2,
  input  in_3,
  output out_4,
  output out_5
);

  wire and_1_out, and_2_out, xor_1_out;

  xor xor_1 (xor_1_out, in_1, in_2);
  and and_1 (and_1_out, in_1, in_2);
  xor xor_2 (out_4, xor_1_out, in_3);
  and and_2 (and_2_out, xor_1_out, in_3);
  or or_1 (out_5, and_2_out, and_1_out);
endmodule

module Pfo3 (
  input  [2:0] A,
  input  [2:0] B,
  output [2:0] Salida,
  output out_4,
  output Flag_Carry,
  output Flag_Zero,
  output out_7
);

  wire sumador_1_out_5, sumador_2_out_5, xnor_1_out, xor_1_out;

  Sumador sumador_1 (.in_1(A[0]), .in_2(B[0]), .in_3(1'b0), .out_4(Salida[0]), .out_5(sumador_1_out_5));
  Sumador sumador_2 (.in_1(A[1]), .in_2(B[1]), .in_3(sumador_1_out_5), .out_4(Salida[1]), .out_5(sumador_2_out_5));
  Sumador sumador_3 (.in_1(A[2]), .in_2(B[2]), .in_3(sumador_2_out_5), .out_4(out_7), .out_5(Flag_Carry));
  // Probe on Salida[0]
  // Probe on Salida[1]
  // Probe on out_7
  nor nor_1 (Flag_Zero, Salida[0], Salida[1], out_7);
  xor xor_1 (xor_1_out, out_7, A[2]);
  and and_1 (out_4, xor_1_out, xnor_1_out);
  xnor xnor_1 (xnor_1_out, A[2], B[2]);

  assign Salida[2] = out_7;

  // Other names for the same wires on the sheet: A_significativo = A[2]; B_significativo = B[2]

  // Notes on the sheet:
  //   Flag Negative
  //   Flag Overflow
endmodule
